# Fritzing sketch 7400 (saved by Fritzing 0.9.4)
breadboards: 1

parts:
  YwRobot_Power_Supply1 = YwRobot Breadboard Power Supply [part_number=545043]
  U1 = 74HC00 [part_number=SN74HC00N package="DIP14 [THT]"]
  R1 = Resistor [tolerance=±5% resistance=10k package=THT]
  R2 = Resistor [tolerance=±5% resistance=10k package=THT]
  C1 = Electrolytic Capacitor [capacitance=1µF package="100 mil [THT, electrolytic]"]
  R3 = Resistor [tolerance=±5% resistance=220 package=THT]
  LED1 = smd LED [color="Red (633nm)" package="0603 [SMD]"]

nets:
  N1: YwRobot_Power_Supply1.VCC#6, U1.2Y, U1.3A, U1.3B, C1.+
  N2: YwRobot_Power_Supply1.GND#11, YwRobot_Power_Supply1.GND#12, U1.GND, LED1.cathode
  N3: U1.1A, U1.1B, R1.Pin_1
  N4: U1.1Y, U1.2A, U1.2B
  N5: U1.3Y, R2.Pin_0, R3.Pin_0
  N6: R1.Pin_0, R2.Pin_1, C1.-
  N7: R3.Pin_1, LED1.anode

custom parts:
  YwRobot Breadboard Power Supply: The YwRobot Breadboard Power Supply (MB-V2) has two power rails; they can be 5V or 3V3. Power to the module can be provided through the female USB socket or through the A10 (female) 2.1mm power jack.
  74HC00: Quad 2 input NAND logic gates.
